# Fritzing sketch Button (saved by Fritzing 0.9.2b)
circuit board: 3.3cm x 3cm
breadboards: 1

parts:
  R4 = Resistor [tolerance=±5% resistance=4.7k package=THT]
  R3 = Resistor [tolerance=±5% resistance=4.7k package=THT]
  Q1 = NPN-Transistor [package="TO92 [THT]"]
  J2 = male pin header, 8 pins [form="♂ (male)"]
  J1 = male pin header, 8 pins [form="♂ (male)"]
  U2 = attiny85 [package=dip]
  U3 = ESP8266 WiFi Module [part_number=ESP8266]
  LED1 = LED - 3mm [color="Red (633nm)" package="3 mm [THT]"]  # not connected
  VCC1 = Battery
  J3 = male pin header, 3 pins [form="♂ (male)"]  # not connected

nets (from the breadboard view):
  N1: R4.Pin_0, U2.Pin_5
  N2: R3.Pin_0, U2.Pin_7
  N3: Q1.E, U2.Pin_4, VCC1.-
  N4: Q1.B, U2.Pin_3
  N5: J2.pin1, U3.VCC
  N6: J2.pin2, U3.GPIO_13
  N7: J2.pin3, U3.GPIO_12
  N8: J2.pin4, U3.GPIO_14
  N9: J2.pin5, U3.GPIO_16
  N10: J2.pin6, U3.CH_PD
  N11: J2.pin7, U3.ADC_0
  N12: J2.pin8, U3.REST
  N13: J1.pin1, U3.GND
  N14: J1.pin2, U3.GPIO_15
  N15: J1.pin3, U3.GPIO_2
  N16: J1.pin4, U3.GPIO_0
  N17: J1.pin5, U3.GPIO_4
  N18: J1.pin6, U3.GPIO_5
  N19: J1.pin7, U3.RXD
  N20: J1.pin8, U3.TXD
  N21: U2.Pin_8, VCC1.+

custom parts:
  ESP8266 WiFi Module: Generic WiFi Module based on the ESP8266 with onboard PCB antenna and UART communications
