# Fritzing sketch Buttonsmall (saved by Fritzing 0.9.2b)
circuit board: 3.3cm x 3.3cm
breadboards: 1

parts:
  Q1 = NPN-Transistor [package="TO92 [THT]"]
  J2 = male pin header, 8 pins [form="♂ (male)"]
  J1 = male pin header, 8 pins [form="♂ (male)"]
  PWR = Battery
  1/2 = male pin header, 3 pins [form="♂ (male)"]
  R1 = Resistor [tolerance=±5% resistance=220 package="0805 [SMD]"]
  LEDPB3 = LED - 3mm [color="Red (633nm)" package="3 mm [THT]"]
  PU = Resistor [tolerance=±5% resistance=10k package="0805 [SMD]"]
  Tiny = attiny85 [package=dip]
  RX/TX = female pin header, 2 pins [form="♀ (female)"]
  PU_2 = Resistor [tolerance=±5% resistance=10k package="0805 [SMD]"]
  C2 = Ceramic Capacitor [capacitance=1µF package="100 mil [THT, multilayer]"]
  PU_3 = Resistor [tolerance=±5% resistance=220 package="0805 [SMD]"]
  U3 = Voltage Regulator - 3.3V [package="TO220 [THT]"]

nets (from the pcb view):
  N1: Q1.B, Tiny.Pin_3
  N2: Q1.C, J2.pin5, J2.pin8
  N3: J2.pin1, J2.pin6, J1.pin3, 1/2.pin2, PU.Pin_0, Tiny.Pin_8, PU_2.Pin_0, PU_3.Pin_1
  N4: J1.pin1, J1.pin2
  N5: J1.pin5, Tiny.Pin_5, PU_2.Pin_1
  N6: J1.pin6, PU.Pin_1, Tiny.Pin_7
  N7: J1.pin7, RX/TX.pin2
  N8: J1.pin8, RX/TX.pin1
  N9: PWR.-, U3.GND
  N10: PWR.+, 1/2.pin1, U3.input_voltage
  N11: 1/2.pin3, C2.1, U3.output_voltage
  N12: R1.Pin_0, LEDPB3.anode
  N13: R1.Pin_1, Tiny.Pin_2

notes:
  pullup
